# Fritzing sketch Circuit_DHT11 (saved by Fritzing 0.9.3b)

parts:
  부품1 = Arduino Uno (Rev3)
  DHT1 = DHT11 Humitidy and Temperature Sensor
  R1 = Resistor [tolerance=±5% resistance=10k package=THT]  # not connected

nets:
  N1: 부품1.D2, DHT1.DATA
  5V: 부품1.5V, DHT1.VDD
  GND: 부품1.GND, DHT1.GND

custom parts:
  DHT11 Humitidy and Temperature Sensor: DHT11 Humidity and Temperature Sensor
