# Fritzing sketch I2CDotMatrix (saved by Fritzing 0.9.3b)

parts:
  부품1 = Arduino Uno (Rev3)
  8x8_LED_Modul_mit_MAX1 = 8x8 LED Modul mit MAX7219 [package=THT]

nets:
  N1: 부품1.D9_PWM, 8x8_LED_Modul_mit_MAX1.CLK_Eingang
  N2: 부품1.D10_PWM/SS, 8x8_LED_Modul_mit_MAX1.CS_Eingang
  N3: 부품1.D12/MISO, 8x8_LED_Modul_mit_MAX1.DIN_Eingang
