# Fritzing sketch main (saved by Fritzing 0.9.3b)
breadboards: 1

parts:
  부품1 = Arduino Uno (Rev3)
  DigitalPushButtonV1 = DigitalPushButtonV2
  DigitalPushButtonV2 = DigitalPushButtonV2
  U1 = L9110 H-bridge module [part_number="L9110 H-bridge"]
  U2 = L9110 H-bridge module [part_number="L9110 H-bridge"]
  M1 = DC Motor
  M2 = DC Motor
  M3 = DC Motor
  M4 = DC Motor
  VCC1 = 4 x AAA Battery Mount
  VCC2 = 4 x AAA Battery Mount  # not connected

nets:
  N1: 부품1.D10_PWM/SS, U2.B-IA
  N2: 부품1.D11_PWM/MOSI, U2.B-IB
  N3: 부품1.D2, DigitalPushButtonV1.Signal
  N4: 부품1.D3_PWM, DigitalPushButtonV2.Signal
  N5: 부품1.D5_PWM, U1.B-IA
  N6: 부품1.D6_PWM, U1.B-IB
  N7: 부품1.5V, DigitalPushButtonV1.Input, DigitalPushButtonV2.Input
  GND: 부품1.GND, DigitalPushButtonV1.GND, DigitalPushButtonV2.GND
  N8: U1.GND, VCC1.-
  N9: U1.MOTOR_A-A, M2.pin_2
  N10: U1.MOTOR_A-B, M2.pin_1
  N11: U1.MOTOR_B-A, M1.pin_2
  N12: U1.MOTOR_B-B, M1.pin_1
  N13: U2.MOTOR_A-A, M4.pin_2
  N14: U2.MOTOR_A-B, M4.pin_1
  N15: U2.MOTOR_B-A, M3.pin_2
  N16: U2.MOTOR_B-B, M3.pin_1
