# Fritzing sketch main (saved by Fritzing 0.9.3b)
breadboards: 1

parts:
  부품1 = Arduino Uno (Rev3)
  부품2 = Bluetooth HC-05 Macho
  M1 = DC Motor
  M2 = DC Motor
  U1 = L9110 H-bridge module [part_number="L9110 H-bridge"]
  VCC2 = Battery
  VCC3 = Battery  # not connected
  VCC4 = Battery  # not connected
  VCC5 = Battery

nets:
  N1: 부품1.D9_PWM, U1.B-IA
  N2: 부품1.D10_PWM/SS, U1.B-IB
  N3: 부품1.D2, 부품2.TXD
  N4: 부품1.D3_PWM, 부품2.RXD
  N5: 부품1.D5_PWM, U1.A-IA
  N6: 부품1.D6_PWM, U1.A-IB
  5V: 부품1.5V, 부품2.VCC
  GND: 부품1.GND, 부품2.GND, U1.GND, VCC2.-
  N7: M1.pin_2, U1.MOTOR_B-A
  N8: M2.pin_1, U1.MOTOR_A-B
  N9: M2.pin_2, U1.MOTOR_A-A
  N10: U1.VCC, VCC5.+
