# Fritzing sketch main (saved by Fritzing 0.9.3b)
breadboards: 1

parts:
  DHT1 = DHT22 Humidity and Temperature Sensor
  부품1 = Arduino Uno (Rev3)
  부품3 = Humidity Sensor - HIH-4030 Breakout
  R1 = Photocell (LDR) [package=THT]
  R2 = Resistor [tolerance=±5% resistance=10k package=THT]
  부품4 = Humidity Sensor - HIH-4030 Breakout
  M1 = DC Motor
  M2 = DC Motor
  KY-1 = Keyes Relay [package=THT]
  KY-2 = Keyes Relay [package=THT]
  BAT1 = Battery Holders [package=battery-aa]
  LED2 = LEDs [package=fkit-led-1206]

nets:
  VCC: DHT1.VDD, 부품1.5V, 부품3.VCC, R1.pin_1, 부품4.VCC, KY-1.power, KY-2.power
  N1: DHT1.DATA, 부품1.D2
  GND: DHT1.GND, 부품1.GND, 부품3.GND, R2.Pin_1, 부품4.GND, M1.pin_2, M2.pin_2, KY-1.ground, KY-2.ground, BAT1.+, LED2.C
  N2: 부품1.A0, 부품3.OUT
  N3: 부품1.A1, R1.pin_0, R2.Pin_0
  N4: 부품1.A2, 부품4.OUT
  N5: 부품1.D10_PWM/SS, M1.pin_1
  N6: 부품1.D11_PWM/MOSI, KY-1.signal
  N7: 부품1.D12/MISO, KY-2.signal
  N8: M2.pin_1, KY-1.NC
  N9: KY-1.C, BAT1.-
  N10: KY-2.NC, LED2.A

notes:
  [CO2 센서 입니다.]
  [수중모터입니다.]
  [쿨러팬입니다.]
  [LED 입니다]
  [모터팬과 LED를 위한 12V LED 입니다.]

custom parts:
  Keyes Relay: The Keyes 5V relay module is suitable for SCM development, home appliance control. It uses a 5V~12V TIL control signal which can control DC / AC signal.
